# Fritzing sketch wiring_mini_cathode (saved by Fritzing 0.9.2b)

parts:
  Power_plug1 = Power plug
  U1 = TOUCH [package=touch1]
  Arduino1 = Arduino Mini (Rev5)
  LED1 = RGB LED (com. anode, rbg) [package="5 mm [THT]"]

nets:
  VCC: Power_plug1.VCC, Arduino1.VCC
  GND: Power_plug1.GND, Arduino1.GND, LED1.common_anode
  N1: U1.T1, Arduino1.D10_PWM
  N2: Arduino1.D3_PWM, LED1.red_cathode
  N3: Arduino1.D5_PWM, LED1.blue_cathode
  N4: Arduino1.D6_PWM, LED1.green_cathode

notes:
  5V
  any metal
  (for touch sensor)
  5V RGB
  Common cathode
