# Fritzing sketch wiring_nano_n_fet (saved by Fritzing 0.9.2b)

parts:
  Power_plug1 = Power plug
  RGB_Strip_LED3 = RGB Strip LED
  Q3 = Basic FET N-Channel [package="DPak [SMD]"]
  Q4 = Basic FET N-Channel [package="DPak [SMD]"]
  Q5 = Basic FET N-Channel [package="DPak [SMD]"]
  Part1 = Arduino Nano (Rev3.0)
  U1 = TOUCH [package=touch1]

nets:
  GND: Power_plug1.GND, Q3.source, Q4.source, Q5.source, Part1.GND
  VCC: Power_plug1.VCC, RGB_Strip_LED3.Common_Connect, Part1.VIN
  N1: RGB_Strip_LED3.Green_Connect, Q4.drain
  N2: RGB_Strip_LED3.Red_Connect, Q3.drain
  N3: RGB_Strip_LED3.Blue_Connect, Q5.drain
  N4: Q3.Gate, Part1.D3
  N5: Q4.Gate, Part1.D5
  N6: Q5.Gate, Part1.D6
  N7: Part1.D10, U1.T1

notes:
  12V
  any metal
  (for touch sensor)
  12V RGB Led Strip

custom parts:
  RGB Strip LED: A tri-color Strip LED with red, green and blue. Based on LED SMD 5050 RGB Pin order: common cathode - green - red - blue
